// Logisim project circuito.circ as structural Verilog: 1 circuit, main circuit main
module main (
  input  A,
  input  B,
  input  C,
  input  D
);

  wire and_1_out, and_2_out, and_3_out, and_4_out, and_5_out, and_6_out, and_7_out, and_8_out, and_9_out,
       and_10_out, and_11_out, and_12_out, and_13_out, and_14_out, and_15_out, and_16_out, and_17_out,
       and_18_out, and_19_out, and_20_out, and_21_out, and_22_out, and_23_out, and_24_out, and_25_out,
       and_26_out, and_27_out, not_1_out, not_2_out, not_3_out, not_4_out, not_5_out, not_6_out, not_7_out,
       not_8_out, not_9_out, not_10_out, not_11_out, or_1_out, or_2_out, or_3_out, or_4_out, or_5_out,
       or_6_out, or_7_out;

  not not_1 (not_1_out, A);
  not not_2 (not_2_out, B);
  not not_3 (not_3_out, C);
  not not_4 (not_4_out, D);
  and and_1 (and_1_out, A, D, not_3_out);
  and and_2 (and_2_out, not_1_out, not_3_out, not_2_out);
  and and_3 (and_3_out, A, B, not_4_out);
  and and_4 (and_4_out, not_1_out, B, C);
  and and_5 (and_5_out, not_1_out, C, not_4_out);
  and and_6 (and_6_out, not_1_out, not_3_out);
  and and_7 (and_7_out, B, not_3_out);
  and and_8 (and_8_out, B, D);
  and and_9 (and_9_out, A, C, D);
  and and_10 (and_10_out, not_1_out, not_2_out);
  and and_11 (and_11_out, C, not_4_out);
  and and_12 (and_12_out, not_1_out, not_4_out);
  and and_13 (and_13_out, not_2_out, not_4_out);
  and and_14 (and_14_out, not_1_out, not_2_out);
  and and_15 (and_15_out, A, B, not_3_out);
  and and_16 (and_16_out, B, not_3_out, D);
  and and_17 (and_17_out, not_2_out, C, not_4_out);
  and and_18 (and_18_out, not_1_out, C, not_4_out);
  and and_19 (and_19_out, not_2_out, D);
  and and_20 (and_20_out, not_1_out, B, C);
  and and_21 (and_21_out, not_1_out, not_2_out, not_3_out);
  and and_22 (and_22_out, A, not_2_out, C);
  and and_23 (and_23_out, A, B, not_3_out, not_4_out);
  and and_24 (and_24_out, not_1_out, not_2_out, not_3_out);
  and and_25 (and_25_out, A, not_2_out, not_4_out);
  and and_26 (and_26_out, A, B, C);
  and and_27 (and_27_out, not_1_out, not_2_out, not_3_out);
  or or_1 (or_1_out, and_24_out, and_26_out, and_25_out);
  or or_2 (or_2_out, and_1_out, and_2_out, and_3_out, and_4_out, and_5_out);
  or or_3 (or_3_out, and_6_out, and_7_out, and_8_out, and_9_out);
  or or_4 (or_4_out, and_10_out, and_11_out, and_12_out, and_13_out);
  or or_5 (or_5_out, and_14_out, and_15_out, and_16_out, and_17_out);
  or or_6 (or_6_out, and_19_out, and_20_out, and_21_out, and_22_out, and_23_out);
  not not_5 (not_5_out, or_1_out);
  or or_7 (or_7_out, D, and_27_out);
  not not_6 (not_6_out, or_2_out);
  not not_7 (not_7_out, or_3_out);
  not not_8 (not_8_out, or_4_out);
  not not_9 (not_9_out, or_5_out);
  not not_10 (not_10_out, or_7_out);
  not not_11 (not_11_out, or_6_out);
  _7_Segment_Display u_7_segment_display_1 (
    .g(not_5_out), .f(not_11_out), .a(not_10_out), .b(not_6_out), .e(not_9_out), .d(not_8_out), .c(not_7_out));  // open: dp

  // Notes on the sheet:
  //   S6
  //   S0
  //   S1
  //   S2
  //   S3
  //   S4
  //   S5
endmodule
